# Fritzing sketch temp (saved by Fritzing 0.9.3b)
breadboards: 1

parts:
  Part1 = Arduino Nano (Rev3.0)
  DHT11_1 = DHT11 module
  LCD1 = LCD screen
  LCM1602_IIC1 = LCM1602 IIC [part_number="LCM1602 IIC" chip_label="LCM1602 IIC" package="DIP (Dual Inline) [THT]"]

nets:
  GND: Part1.GND, DHT11_1.GND, LCM1602_IIC1.GND
  N1: Part1.D2, DHT11_1.DATA
  VCC: Part1.5V, DHT11_1.VCC, LCM1602_IIC1.VCC
  N2: Part1.A5, LCM1602_IIC1.SCL
  N3: Part1.A4, LCM1602_IIC1.SDA
  VSS: LCD1.VSS, LCM1602_IIC1.VSS
  VDD: LCD1.VDD, LCM1602_IIC1.VDD
  N4: LCD1.V0, LCM1602_IIC1.V0
  N5: LCD1.RS, LCM1602_IIC1.RS
  N6: LCD1.R/W, LCM1602_IIC1.RW
  N7: LCD1.E, LCM1602_IIC1.E
  N8: LCD1.DB0, LCM1602_IIC1.D0
  N9: LCD1.DB1, LCM1602_IIC1.D1
  N10: LCD1.DB2, LCM1602_IIC1.D2
  N11: LCD1.DB3, LCM1602_IIC1.D3
  N12: LCD1.DB4, LCM1602_IIC1.D4
  N13: LCD1.DB5, LCM1602_IIC1.D5
  N14: LCD1.DB6, LCM1602_IIC1.D6
  N15: LCD1.DB7, LCM1602_IIC1.D7
  N16: LCD1.LED+, LCM1602_IIC1.A
  N17: LCD1.LED-, LCM1602_IIC1.K

custom parts:
  DHT11 module: https://cdn-learn.adafruit.com/downloads/pdf/dht.pdf DHT11 black pcb module reference by:https://github.com/adafruit/Fritzing-Library/blob/master/parts/DHT11%20Humitidy%20and%20Temperature%20Sensor.fzpz
  LCM1602 IIC: I2C-Module to use a 1602 or 2004 LCD on with the wire.h libory Serial LCD Modul

// code stored in the sketch: Untitled2.ino
#include <Wire.h>
#include <LiquidCrystal_I2C.h>
#include "DHT.h"


#define DHTPIN 2        // Data pin for the DHT sensor
#define DHTTYPE DHT11   // Change to DHT22 if using that sensor


DHT dht(DHTPIN, DHTTYPE);
LiquidCrystal_I2C lcd(0x27, 16, 2); // Use 0x3F if 0x27 doesn?t work


void setup() {
  lcd.init();          // Initialize LCD
  lcd.backlight();     // Turn on backlight
  dht.begin();         // Start DHT sensor
  lcd.setCursor(0, 0);
  lcd.print("Sensor OK");
  delay(1000);
  lcd.clear();
}


void loop() {
  float t = dht.readTemperature();  // Temperature in Celsius
  float h = dht.readHumidity();     // Humidity in percentage


  if (isnan(t) || isnan(h)) {
    lcd.setCursor(0, 0);
    lcd.print("Error reading");
    lcd.setCursor(0, 1);
    lcd.print("sensor data");
  } else {
    lcd.setCursor(0, 0);
    lcd.print("Temp: ");
    lcd.print(t);
    lcd.print((char)223); // Degree symbol
    lcd.print("C");


    lcd.setCursor(0, 1);
    lcd.print("Humidity: ");
    lcd.print(h);
    lcd.print("%  ");
  }
  delay(2000); // Update every 2 seconds
}
